# Fritzing sketch Schema (saved by Fritzing 0.9.3b)
breadboards: 1

parts:
  Onderdeel2 = Arduino Nano (Rev3.0)
  LED1 = LED - 5mm [color="Red (633nm)" package="5 mm [THT]"]
  LED2 = LED - 5mm [color="Green (555nm)" package="5 mm [THT]"]
  R1 = Resistor [tolerance=±5% resistance=220 package="0402 [SMD]"]
  R2 = Resistor [tolerance=±5% resistance=220 package="0402 [SMD]"]
  HC-SR04_Sensor_1 = HC-SR04 Ultrasonic Distance Sensor
  SP1 = SPEAKER [package=pcb_mount_speaker]
  100 = Resistor [tolerance=±5% resistance=100 package="0402 [SMD]"]

nets:
  GND: Onderdeel2.GND, LED1.cathode, LED2.cathode, HC-SR04_Sensor_1.GND, 100.Pin_0
  N1: Onderdeel2.D4, R2.Pin_0
  N2: Onderdeel2.D5, R1.Pin_0
  N3: Onderdeel2.D8, SP1.-
  N4: Onderdeel2.D9, HC-SR04_Sensor_1.TRIG
  N5: Onderdeel2.D10, HC-SR04_Sensor_1.ECHO
  N6: LED1.anode, R2.Pin_1
  N7: LED2.anode, R1.Pin_1
  N8: SP1.+, 100.Pin_1
